# Fritzing sketch I-GAUGE COMPLETE VERSION (saved by Fritzing 0.9.3b)

parts:
  HopeRF_LoRa_RFM9X = Adafruit RFM9x LoRa Radio [part_number="Adafruit #3072 and #3073"]
  Part3 = Arduino Mega 2560 (Rev3)
  DS18B20 = DS18B20 1-Wire Temperature Sensor [part_number=DS18B20]
  Part4 = Logic Level Converter
  SIM800L = SIM800L [package=THT]
  GPS_U-BLOX_NE0-6M = Adafruit Ultimate GPS v3 [part_number="Adafruit #746"]
  WeMos_D1_Data_Logger_Shield = WeMos D1 Mini Micro SD Shield
  WeMos_D1_Mini1 = WeMos D1 Mini
  RELAY_WEMOS = DS2Y-5-DC5V [part_number=DS2Y-5-DC5V]
  ADS1115 = Adafruit ADS1115 16Bit I2C ADC [part_number="Adafruit #1085"]
  ACS712_5A = ACS712 Low Current Sensor Board v12
  MPX4250AP1 = MPX4250AP pressure sensor [part_number=MPX]
  Power_plug1 = Power plug
  D1 = Rectifier Diode [part_number=1N4001 package="300 mil [THT]"]
  R1 = Resistor [tolerance=±5% resistance=220 package=THT]
  Q1 = NPN-Transistor [package="TO92 [THT]"]
  relay_power = DS2Y-5-DC5V [part_number=DS2Y-5-DC5V]
  D2 = Rectifier Diode [part_number=1N4001 package="300 mil [THT]"]
  Part8 = Adafruit USB DC Solar LiPo Charger [part_number="Adafruit #390"]
  Part9 = Lithium Ion Cylindrical Battery 3.7v 2200mAh [part_number=1781]
  Part10 = Lithium Ion Cylindrical Battery 3.7v 2200mAh [part_number=1781]
  Part11 = Lithium Ion Cylindrical Battery 3.7v 2200mAh [part_number=1781]
  Part12 = Lithium Ion Cylindrical Battery 3.7v 2200mAh [part_number=1781]
  step_down = RioRand LM2596
  step_up = RioRand LM2596
  Voltage_sensor = Resistor [tolerance=±5% resistance=20k package=THT]
  R3 = Resistor [tolerance=±5% resistance=10k package=THT]
  D3 = Rectifier Diode [part_number=1N4001 package="300 mil [THT]"]
  Fuse1 = Fuse with Handler [part_number=Htc-15m]
  7805 = Voltage Regulator [package=78xxl]
  C1 = Electrolytic Capacitor [capacitance=1000µF package="300 mil [THT, electrolytic]"]
  C2 = Electrolytic Capacitor [capacitance=1000µF package="300 mil [THT, electrolytic]"]
  C3 = Ceramic Capacitor [capacitance=100nF package="100 mil [THT, multilayer]"]
  Fuse2 = Fuse with Handler [part_number=Htc-15m]
  LM317 = Voltage Regulator [package=to220-adj]
  C4 = Ceramic Capacitor [capacitance=100nF package="100 mil [THT, multilayer]"]
  Part13 = DeuLigne 1.1 - The Snootlab's LCD shield for Arduino
  LED_POWER = RGB LED - (4 legs) [package="5 mm [THT]"]
  LED_STATUS = RGB LED - (4 legs) [package="5 mm [THT]"]
  Part14 = Logic Level Converter
  Q2 = NPN-Transistor [package="TO92 [THT]"]
  D4 = Rectifier Diode [part_number=1N4001 package="300 mil [THT]"]
  R4 = Resistor [tolerance=±5% resistance=220 package=THT]

nets:
  3V3: HopeRF_LoRa_RFM9X.VIN, Part4.LV, WeMos_D1_Data_Logger_Shield.3V3, WeMos_D1_Mini1.3V3, LM317.OUT, C4.0, Part14.LV
  GND: HopeRF_LoRa_RFM9X.GND, Part3.GND, DS18B20.GND, Part4.GND, SIM800L.GND, GPS_U-BLOX_NE0-6M.GND, WeMos_D1_Data_Logger_Shield.G, WeMos_D1_Mini1.G, ADS1115.ADDR, ADS1115.GND, ACS712_5A.GND, MPX4250AP1.GND, Power_plug1.GND, Q1.E, Part8.GND, Part10.negative, Part12.negative, step_down.Pin_3, step_up.Pin_3, R3.Pin_1, 7805.GND, C1.-, C2.-, C3.0, LM317.ADJ, C4.1, Part13.GND, Part14.GND, Q2.E
  N1: HopeRF_LoRa_RFM9X.SCK, Part4.RX_LV, WeMos_D1_Data_Logger_Shield.D5
  N2: HopeRF_LoRa_RFM9X.MISO, Part4.TX2_LV, WeMos_D1_Data_Logger_Shield.D6
  N3: HopeRF_LoRa_RFM9X.MOSI, Part4.RX2_LV, WeMos_D1_Data_Logger_Shield.D7
  N4: HopeRF_LoRa_RFM9X.CS, Part14.RX2_LV
  N5: Part3.D21/SCL, WeMos_D1_Data_Logger_Shield.D1, ADS1115.SCL, Part13.A5(CLK)
  N6: Part3.D20/SDA, WeMos_D1_Data_Logger_Shield.D2, ADS1115.SDA, Part13.A4(SDA)
  N7: Part3.D19/RX1, SIM800L.SIM_TXD
  N8: Part3.D18/TX1, SIM800L.SIM_RXD
  N9: Part3.D17_PWM/RX2, GPS_U-BLOX_NE0-6M.TX
  N10: Part3.D16_PWM/TX2, GPS_U-BLOX_NE0-6M.RX
  N11: Part3.D15/RX3, Part14.TX_HV
  N12: Part3.D14/TX3, Part14.RX_HV
  N13: Part3.D10_PWM, Part14.RX2_HV
  N14: Part3.VIN, Fuse1.Connector2
  N15: Part3.D3_PWM, R4.Pin_0
  5V: Part3.5V, Part13.+5V
  N16: Part3.D30, DS18B20.DQ
  N17: Part3.D32, LED_POWER.green_cathode
  N18: Part3.D34, LED_POWER.blue_cathode
  N19: Part3.D36, LED_STATUS.red_cathode
  N20: Part3.D38, LED_STATUS.green_cathode
  N21: Part3.D40, LED_STATUS.blue_cathode
  N22: Part3.D50, Part4.TX2_HV
  N23: Part3.D51, Part4.RX2_HV
  N24: Part3.D52, Part4.RX_HV
  N25: Part3.D53, Part4.TX_HV
  VDD: DS18B20.VDD, Part4.HV, GPS_U-BLOX_NE0-6M.VIN, WeMos_D1_Data_Logger_Shield.5V, RELAY_WEMOS.16_-, RELAY_WEMOS.13_COM, ADS1115.VDD, ACS712_5A.5V, MPX4250AP1.Vs, Fuse2.Connector2, LED_POWER.common_anode, LED_STATUS.common_anode, Part14.HV, D4.cathode
  N26: Part4.TX_LV, WeMos_D1_Data_Logger_Shield.D8
  N27: SIM800L.5V, step_down.Pin_2
  N28: WeMos_D1_Mini1.5V, RELAY_WEMOS.9_N.O.
  N29: WeMos_D1_Mini1.RX, Part14.RX_LV
  N30: WeMos_D1_Mini1.TX, Part14.TX_LV
  N31: RELAY_WEMOS.1_+, Q2.C, D4.anode
  N32: ADS1115.AIN3, MPX4250AP1.V_out
  N33: ADS1115.AIN1, Voltage_sensor.Pin_1, R3.Pin_0
  N34: ADS1115.AIN0, ACS712_5A.VO
  N35: ACS712_5A.IP+, Part8.LOAD
  N36: ACS712_5A.IP-, relay_power.4_COM
  N37: Power_plug1.VCC, D1.anode, relay_power.16_-, relay_power.13_COM, D2.cathode, Part8.DCIN
  N38: D1.cathode, R1.Pin_0
  N39: R1.Pin_1, Q1.B
  N40: Q1.C, relay_power.1_+, D2.anode
  N41: relay_power.6_N.C., relay_power.9_N.O., step_up.Pin_0, Voltage_sensor.Pin_0
  N42: Part8.BATT, Part9.positive, Part11.positive
  N43: Part9.negative, Part10.positive
  N44: Part11.negative, Part12.positive
  N45: step_up.Pin_2, D3.cathode, 7805.IN, C1.+, LM317.IN
  N46: D3.anode, Fuse1.Connector1
  N47: 7805.OUT, C2.+, C3.1, Fuse2.Connector1
  N48: Q2.B, R4.Pin_1

custom parts:
  Adafruit RFM9x LoRa Radio: Sending data over long distances is like magic, and now you can be a magician with this range of powerful and easy-to-use radio modules. Sure, sometimes you want to talk to a computer (a good time to use WiFi) or perhaps communicate with a Phone (choose Bluetooth Low Energy!) but what if you want to send data very far? Most WiFi, Bluetooth, Zigbee and other wireless chipsets use 2.4GHz, which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
  Adafruit Ultimate GPS v3: We carry a few different GPS modules here in the Adafruit shop, but none that satisfied our every desire - that's why we designed this little GPS breakout board. We believe this is the Ultimate GPS module, so we named it that. It's got everything you want and more: -165 dBm sensitivity, 10 Hz updates, 66 channels 5V friendly design and only 20mA current draw Breadboard friendly + two mounting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
  Adafruit ADS1115 16Bit I2C ADC: For microcontrollers without an analog-to-digital converter or when you want a higher-precision ADC, the ADS1115 provides 16-bit precision at 860 samples/second over I2C. The chip can be configured as 4 single-ended input channels, or two differential channels. As a nice bonus, it even includes a programmable gain amplifier, up to x16, to help boost up smaller single/differential signals to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
  Adafruit USB DC Solar LiPo Charger: Make your projects to go green this summer with our specialized USB/Solar Lithium Ion Polymer Battery charger! This charger is a very unique design, perfect for outdoor projects, or DIY iPod chargers. We've spent over a year testing and tinkering with this charger to come up with a plug and play solution to charging batteries with the sun and we're really pleased with what we ended up with.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
  Lithium Ion Cylindrical Battery 3.7v 2200mAh: This lithium ion battery has a capacity of 2200mAh and a protection circuit that provides over-voltage, under-voltage and over-current protection. This cell can provide 2C of peak current (4400mA). Note that these batteries are not designed to sustain such high loads, we suggest keeping any constant current draw under about 0.5C (1 Amp).
