# Fritzing sketch i-gauge LoRa Gateway (saved by Fritzing 0.9.3b)

parts:
  HopeRF_LoRa_RFM9X = Adafruit RFM9x LoRa Radio [part_number="Adafruit #3072 and #3073"]
  Part3 = Arduino Mega 2560 (Rev3)
  Part4 = Logic Level Converter
  SIM800L = SIM800L [package=THT]
  WeMos_D1_Data_Logger_Shield = WeMos D1 Mini Micro SD Shield
  Power_plug1 = Power plug
  D1 = Rectifier Diode [part_number=1N4001 package="300 mil [THT]"]
  R1 = Resistor [tolerance=±5% resistance=220 package=THT]
  Q1 = NPN-Transistor [package="TO92 [THT]"]
  relay_power = DS2Y-5-DC5V [part_number=DS2Y-5-DC5V]
  D2 = Rectifier Diode [part_number=1N4001 package="300 mil [THT]"]
  Part8 = Adafruit USB DC Solar LiPo Charger [part_number="Adafruit #390"]
  Part9 = Lithium Ion Cylindrical Battery 3.7v 2200mAh [part_number=1781]
  Part10 = Lithium Ion Cylindrical Battery 3.7v 2200mAh [part_number=1781]
  Part11 = Lithium Ion Cylindrical Battery 3.7v 2200mAh [part_number=1781]
  Part12 = Lithium Ion Cylindrical Battery 3.7v 2200mAh [part_number=1781]
  step_down = RioRand LM2596
  step_up = RioRand LM2596
  D3 = Rectifier Diode [part_number=1N4001 package="300 mil [THT]"]
  Fuse1 = Fuse with Handler [part_number=Htc-15m]
  7805 = Voltage Regulator [package=78xxl]
  C1 = Electrolytic Capacitor [capacitance=1000µF package="300 mil [THT, electrolytic]"]
  C2 = Electrolytic Capacitor [capacitance=1000µF package="300 mil [THT, electrolytic]"]
  C3 = Ceramic Capacitor [capacitance=100nF package="100 mil [THT, multilayer]"]
  Fuse2 = Fuse with Handler [part_number=Htc-15m]
  LM317 = Voltage Regulator [package=to220-adj]
  C4 = Ceramic Capacitor [capacitance=100nF package="100 mil [THT, multilayer]"]
  Part13 = DeuLigne 1.1 - The Snootlab's LCD shield for Arduino
  Part14 = Logic Level Converter
  LED_STATUS = RGB LED - (4 legs) [package="5 mm [THT]"]

nets:
  VIN: HopeRF_LoRa_RFM9X.VIN, Part4.LV, WeMos_D1_Data_Logger_Shield.3V3, LM317.OUT, C4.0, Part14.LV
  GND: HopeRF_LoRa_RFM9X.GND, Part3.GND, Part4.GND, SIM800L.GND, WeMos_D1_Data_Logger_Shield.G, step_down.Pin_3, step_up.Pin_3, 7805.GND, C1.-, C2.-, C3.0, LM317.ADJ, C4.1, Part13.GND, Part14.GND
  N1: HopeRF_LoRa_RFM9X.SCK, Part4.RX_LV, WeMos_D1_Data_Logger_Shield.D5
  N2: HopeRF_LoRa_RFM9X.MISO, Part4.TX2_LV, WeMos_D1_Data_Logger_Shield.D6
  N3: HopeRF_LoRa_RFM9X.MOSI, Part4.RX2_LV, WeMos_D1_Data_Logger_Shield.D7
  N4: HopeRF_LoRa_RFM9X.CS, Part14.TX2_LV, Part14.RX2_LV
  N5: Part3.D21/SCL, WeMos_D1_Data_Logger_Shield.D1, Part13.A5(CLK)
  N6: Part3.D20/SDA, WeMos_D1_Data_Logger_Shield.D2, Part13.A4(SDA)
  N7: Part3.D19/RX1, SIM800L.SIM_TXD
  N8: Part3.D18/TX1, SIM800L.SIM_RXD
  N9: Part3.D10_PWM, Part14.RX2_HV, Part14.TX2_HV
  N10: Part3.VIN, Fuse1.Connector2
  5V: Part3.5V, Part13.+5V
  N11: Part3.D36, LED_STATUS.red_cathode
  N12: Part3.D38, LED_STATUS.green_cathode
  N13: Part3.D40, LED_STATUS.blue_cathode
  N14: Part3.D50, Part4.TX2_HV
  N15: Part3.D51, Part4.RX2_HV
  N16: Part3.D52, Part4.RX_HV
  N17: Part3.D53, Part4.TX_HV
  N18: Part4.TX_LV, WeMos_D1_Data_Logger_Shield.D8
  N19: Part4.HV, WeMos_D1_Data_Logger_Shield.5V, Fuse2.Connector2, LED_STATUS.common_anode
  N20: SIM800L.5V, step_down.Pin_2
  GND_2: Power_plug1.GND, Q1.E, Part8.GND, Part10.negative, Part12.negative
  N21: Power_plug1.VCC, D1.anode, relay_power.16_-, relay_power.13_COM, D2.cathode, Part8.DCIN
  N22: D1.cathode, R1.Pin_0
  N23: R1.Pin_1, Q1.B
  N24: Q1.C, relay_power.1_+, D2.anode
  N25: relay_power.6_N.C., relay_power.9_N.O., step_up.Pin_0
  N26: relay_power.4_COM, Part8.LOAD
  N27: Part8.BATT, Part9.positive, Part11.positive
  N28: Part9.negative, Part10.positive
  N29: Part11.negative, Part12.positive
  N30: step_up.Pin_2, D3.cathode, 7805.IN, C1.+, LM317.IN
  N31: D3.anode, Fuse1.Connector1
  N32: 7805.OUT, C2.+, C3.1, Fuse2.Connector1

custom parts:
  Adafruit RFM9x LoRa Radio: Sending data over long distances is like magic, and now you can be a magician with this range of powerful and easy-to-use radio modules. Sure, sometimes you want to talk to a computer (a good time to use WiFi) or perhaps communicate with a Phone (choose Bluetooth Low Energy!) but what if you want to send data very far? Most WiFi, Bluetooth, Zigbee and other wireless chipsets use 2.4GHz, which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
  Adafruit USB DC Solar LiPo Charger: Make your projects to go green this summer with our specialized USB/Solar Lithium Ion Polymer Battery charger! This charger is a very unique design, perfect for outdoor projects, or DIY iPod chargers. We've spent over a year testing and tinkering with this charger to come up with a plug and play solution to charging batteries with the sun and we're really pleased with what we ended up with.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
  Lithium Ion Cylindrical Battery 3.7v 2200mAh: This lithium ion battery has a capacity of 2200mAh and a protection circuit that provides over-voltage, under-voltage and over-current protection. This cell can provide 2C of peak current (4400mA). Note that these batteries are not designed to sustain such high loads, we suggest keeping any constant current draw under about 0.5C (1 Amp).
